// Logisim project T1Final.circ as structural Verilog: 5 circuits, main circuit main
module main (
  input  [7:0] in_1,
  input  clear,
  input  [7:0] in_3,
  input  D,
  input  clear_2,
  input  select_1,
  input  select_0,
  input  Binvert
);

  wire and_1_out, clock_out, d_ff_1_q, fa_1_carryout, fa_1_s, mux4x1_1_q, or_1_out, xor_1_out, xor_2_out;
  wire [3:0] registradoresa_1_q0, registradoresa_1_q4, registradoresb_1_q0, registradoresb_1_q4;

  Clock clock (.out(clock_out));
  registradoresB registradoresb_1 (
    .D7(D), .clock(clock_out), .clear(clear_2), .Q7(registradoresb_1_q4[3]), .Q6(registradoresb_1_q4[2]),
    .Q5(registradoresb_1_q4[1]), .Q4(registradoresb_1_q4[0]), .Q3(registradoresb_1_q0[3]),
    .Q2(registradoresb_1_q0[2]), .Q1(registradoresb_1_q0[1]), .Q0(registradoresb_1_q0[0]), .preset7(in_3[7]),
    .preset6(in_3[6]), .preset5(in_3[5]), .preset4(in_3[4]), .preset3(in_3[3]), .preset2(in_3[2]),
    .preset1(in_3[1]), .preset0(in_3[0]));
  Hex_Digit_Display hex_digit_display_1 (.value(registradoresb_1_q4));  // open: dp
  Hex_Digit_Display hex_digit_display_2 (.value(registradoresb_1_q0));  // open: dp
  registradoresA registradoresa_1 (
    .D7(mux4x1_1_q), .clock(clock_out), .clear(clear), .Q7(registradoresa_1_q4[3]),
    .Q6(registradoresa_1_q4[2]), .Q5(registradoresa_1_q4[1]), .Q4(registradoresa_1_q4[0]),
    .Q3(registradoresa_1_q0[3]), .Q2(registradoresa_1_q0[2]), .Q1(registradoresa_1_q0[1]),
    .Q0(registradoresa_1_q0[0]), .preset7(in_1[7]), .preset6(in_1[6]), .preset5(in_1[5]), .preset4(in_1[4]),
    .preset3(in_1[3]), .preset2(in_1[2]), .preset1(in_1[1]), .preset0(in_1[0]));
  Hex_Digit_Display hex_digit_display_3 (.value(registradoresa_1_q4));  // open: dp
  xor xor_1 (xor_1_out, registradoresb_1_q0[0], Binvert);
  Hex_Digit_Display hex_digit_display_4 (.value(registradoresa_1_q0));  // open: dp
  and and_1 (and_1_out, registradoresa_1_q0[0], registradoresb_1_q0[0]);
  or or_1 (or_1_out, registradoresa_1_q0[0], registradoresb_1_q0[0]);
  xor xor_2 (xor_2_out, registradoresa_1_q0[0], registradoresb_1_q0[0]);
  FA fa_1 (.A(registradoresa_1_q0[0]), .B(xor_1_out), .CarryIn(d_ff_1_q), .S(fa_1_s), .CarryOut(fa_1_carryout));
  D_Flip_Flop d_ff_1 (.clk(clock_out), .D(fa_1_carryout), .Q(d_ff_1_q));  // open: Qn, preset, en, reset
  MUX4X1 mux4x1_1 (
    .d_0(and_1_out), .d_1(or_1_out), .d_2(xor_2_out), .d_3(fa_1_s), .select_1(select_1), .select_0(select_0),
    .q(mux4x1_1_q));

  // Notes on the sheet:
  //   Carolina Ferreira & Mateus Caçabuena
endmodule

module FA (
  input  A,
  input  B,
  input  CarryIn,
  output S,
  output CarryOut
);

  wire and_1_out, and_2_out, xor_1_out;

  xor xor_1 (xor_1_out, A, B);
  xor xor_2 (S, xor_1_out, CarryIn);
  and and_1 (and_1_out, CarryIn, xor_1_out);
  and and_2 (and_2_out, A, B);
  or or_1 (CarryOut, and_1_out, and_2_out);

  // Notes on the sheet:
  //   Full Adder (Somador de 1bit) - Aula 05, slide 9/11
endmodule

module MUX4X1 (
  input  select_1,
  input  select_0,
  input  d_0,
  input  d_1,
  input  d_2,
  input  d_3,
  output q
);

  wire and_1_out, and_2_out, and_3_out, and_4_out, not_1_out, not_2_out;

  not not_1 (not_1_out, select_1);
  not not_2 (not_2_out, select_0);
  and and_1 (and_1_out, d_0, not_1_out, not_2_out);
  and and_2 (and_2_out, d_1, not_1_out, select_0);
  and and_3 (and_3_out, d_2, select_1, not_2_out);
  and and_4 (and_4_out, d_3, select_1, select_0);
  or or_1 (q, and_1_out, and_2_out, and_3_out, and_4_out);

  // Notes on the sheet:
  //   Multiplexador 4x1 - Aula 05, slide 6/11
endmodule

// A
module registradoresA (
  input  D7,
  input  clock,
  input  clear,
  input  preset7,
  input  preset6,
  input  preset5,
  input  preset4,
  input  preset3,
  input  preset2,
  input  preset1,
  input  preset0,
  output Q7,
  output Q6,
  output Q5,
  output Q4,
  output Q3,
  output Q2,
  output Q1,
  output Q0
);

  D_Flip_Flop d_ff_1 (.clk(clock), .D(D7), .Q(Q7), .preset(preset7), .reset(clear));  // open: Qn, en
  D_Flip_Flop d_ff_2 (.clk(clock), .D(Q7), .Q(Q6), .preset(preset6), .reset(clear));  // open: Qn, en
  D_Flip_Flop d_ff_3 (.clk(clock), .D(Q6), .Q(Q5), .preset(preset5), .reset(clear));  // open: Qn, en
  D_Flip_Flop d_ff_4 (.clk(clock), .D(Q5), .Q(Q4), .preset(preset4), .reset(clear));  // open: Qn, en
  D_Flip_Flop d_ff_5 (.clk(clock), .D(Q4), .Q(Q3), .preset(preset3), .reset(clear));  // open: Qn, en
  D_Flip_Flop d_ff_6 (.clk(clock), .D(Q3), .Q(Q2), .preset(preset2), .reset(clear));  // open: Qn, en
  D_Flip_Flop d_ff_7 (.clk(clock), .D(Q2), .Q(Q1), .preset(preset1), .reset(clear));  // open: Qn, en
  D_Flip_Flop d_ff_8 (.clk(clock), .D(Q1), .Q(Q0), .preset(preset0), .reset(clear));  // open: Qn, en
endmodule

// B
module registradoresB (
  input  D7,
  input  clock,
  input  clear,
  input  preset7,
  input  preset6,
  input  preset5,
  input  preset4,
  input  preset3,
  input  preset2,
  input  preset1,
  input  preset0,
  output Q7,
  output Q6,
  output Q5,
  output Q4,
  output Q3,
  output Q2,
  output Q1,
  output Q0
);

  D_Flip_Flop d_ff_1 (.clk(clock), .D(D7), .Q(Q7), .preset(preset7), .reset(clear));  // open: Qn, en
  D_Flip_Flop d_ff_2 (.clk(clock), .D(Q7), .Q(Q6), .preset(preset6), .reset(clear));  // open: Qn, en
  D_Flip_Flop d_ff_3 (.clk(clock), .D(Q6), .Q(Q5), .preset(preset5), .reset(clear));  // open: Qn, en
  D_Flip_Flop d_ff_4 (.clk(clock), .D(Q5), .Q(Q4), .preset(preset4), .reset(clear));  // open: Qn, en
  D_Flip_Flop d_ff_5 (.clk(clock), .D(Q4), .Q(Q3), .preset(preset3), .reset(clear));  // open: Qn, en
  D_Flip_Flop d_ff_6 (.clk(clock), .D(Q3), .Q(Q2), .preset(preset2), .reset(clear));  // open: Qn, en
  D_Flip_Flop d_ff_7 (.clk(clock), .D(Q2), .Q(Q1), .preset(preset1), .reset(clear));  // open: Qn, en
  D_Flip_Flop d_ff_8 (.clk(clock), .D(Q1), .Q(Q0), .preset(preset0), .reset(clear));  // open: Qn, en
endmodule
